// Logisim project SAP1.circ as structural Verilog: 3 circuits, main circuit main
module main (
  output [7:0] out_1
);

  wire clock_1_out;

  Clock clock_1 (.out(clock_1_out));
  ProgramCounter programcounter_1 (.Ep(1'b1), .CLK(clock_1_out), .PC(out_1));  // open: Cp, CLR_INV
  MAR mar_1 ();  // open: WBus, Lm, CLK
endmodule

module ProgramCounter (
  input  Ep,
  input  Cp,
  input  CLK,
  input  CLR_INV,
  output [7:0] PC
);

  wire not_1_out, not_2_out, not_3_out, not_4_out;
  wire [7:0] c74LS126_q;

  not not_1 (not_1_out, CLK);
  J_K_Flip_Flop c74LS126 (.J(1'b1), .K(1'b1), .clk(not_1_out), .Q(c74LS126_q[0]), .reset(CLR_INV));  // open: Qn, preset
  not not_2 (not_2_out, c74LS126_q[0]);
  J_K_Flip_Flop j_k_ff_1 (.J(1'b1), .K(1'b1), .clk(not_2_out), .Q(c74LS126_q[1]), .reset(CLR_INV));  // open: Qn, preset
  not not_3 (not_3_out, c74LS126_q[1]);
  J_K_Flip_Flop j_k_ff_2 (.J(1'b1), .K(1'b1), .clk(not_3_out), .Q(c74LS126_q[2]), .reset(CLR_INV));  // open: Qn, preset
  not not_4 (not_4_out, c74LS126_q[2]);
  J_K_Flip_Flop j_k_ff_3 (.J(1'b1), .K(1'b1), .clk(not_4_out), .Q(c74LS126_q[3]));  // open: Qn, preset, reset
  assign PC = Ep ? c74LS126_q : 8'bz;  // Controlled_Buffer controlled_buffer_1
endmodule

module MAR (
  input  [7:0] WBus,
  input  Lm,
  input  CLK
);

  wire RUN_PROG_sw2;
  wire [3:0] ADDRESS_sw4, c74LS173_q, controlled_buffer_1_out, multiplexer_1_out;
  wire [7:0] DATA_sw8;

  // Probe on controlled_buffer_1_out
  assign controlled_buffer_1_out = Lm ? WBus[3:0] : 4'bz;  // Controlled_Buffer controlled_buffer_1
  DipSwitch #(.number(4)) ADDRESS (
    .sw1(ADDRESS_sw4[3]), .sw2(ADDRESS_sw4[2]), .sw3(ADDRESS_sw4[1]), .sw4(ADDRESS_sw4[0]));
  Register #(.width(4)) c74LS173 (.D(controlled_buffer_1_out), .en(1'b1), .clk(CLK), .Q(c74LS173_q), .clr(1'b0));
  DipSwitch DATA (
    .sw1(DATA_sw8[7]), .sw2(DATA_sw8[6]), .sw3(DATA_sw8[5]), .sw4(DATA_sw8[4]), .sw5(DATA_sw8[3]),
    .sw6(DATA_sw8[2]), .sw7(DATA_sw8[1]), .sw8(DATA_sw8[0]));
  // Probe on multiplexer_1_out
  DipSwitch #(.number(2)) RUN_PROG (.sw2(RUN_PROG_sw2));  // open: sw1
  Multiplexer #(.width(4), .enable("false")) multiplexer_1 (
    .in0(c74LS173_q), .in1(ADDRESS_sw4), .out(multiplexer_1_out), .sel(RUN_PROG_sw2));
  RAM #(.addrWidth(4)) ram_1 (.addr(multiplexer_1_out), .clk(CLK), .data(DATA_sw8));  // open: we, oe
endmodule
